// Logisim project lab simulation.circ as structural Verilog: 1 circuit, main circuit main
module main (
  input  in_1,
  input  in_2,
  input  in_3,
  input  in_4
);

  wire nor_1_out, nor_2_out, nor_3_out, nor_4_out, nor_5_out, nor_6_out, nor_7_out, nor_8_out, nor_9_out,
       nor_10_out, nor_11_out, nor_12_out, nor_13_out, nor_14_out, nor_18_out, nor_19_out, undriven,
       undriven_2, undriven_3, undriven_4, undriven_5, undriven_6, undriven_7, undriven_8, undriven_9,
       undriven_10;

  nor nor_1 (nor_1_out, in_1, in_1);
  nor nor_2 (nor_2_out, in_2, in_2);
  nor nor_3 (nor_3_out, in_3, in_3);
  nor nor_4 (nor_4_out, in_4, in_4);
  nor nor_5 (nor_5_out, undriven_4, undriven_4);
  nor nor_6 (nor_6_out, undriven_5, undriven_5);
  nor nor_7 (nor_7_out, undriven_6, undriven_6);
  nor nor_8 (nor_8_out, undriven_7, undriven_7);
  nor nor_9 (nor_9_out, undriven_8, undriven_8);
  nor nor_10 (nor_10_out, undriven_9, undriven_9);
  nor nor_11 (nor_11_out, undriven_2, undriven_2);
  nor nor_12 (nor_12_out, undriven_3, undriven_3);
  nor nor_13 (nor_13_out, undriven, undriven);
  // NOR_Gate nor_14 has open pins: out=nor_14_out
  // NOR_Gate nor_15 is placed but not wired
  // NOR_Gate nor_16 is placed but not wired
  // NOR_Gate nor_17 is placed but not wired
  nor nor_18 (nor_18_out, undriven_10, undriven_10);
  // NOR_Gate nor_19 has open pins: out=nor_19_out
  // NOR_Gate nor_20 has open pins: in0=nor_5_out, in1=nor_6_out, out=open
  // NOR_Gate nor_21 has open pins: in0=nor_7_out, in1=nor_18_out, in2=nor_8_out, out=open
  // NOR_Gate nor_22 has open pins: in0=nor_9_out, in1=nor_10_out, out=open
  // NOR_Gate nor_23 has open pins: in0=nor_11_out, in1=nor_12_out, out=open
  // NOR_Gate nor_24 has open pins: in0=nor_13_out, in1=nor_19_out, in2=nor_14_out, out=open
  // NOR_Gate nor_25 is placed but not wired
endmodule
